# Fritzing sketch Atomizer Chuff 555 v2 (saved by Fritzing 1.0.6)

parts:
  M4 = seeed grove atomizer v1.0
  U2 = Mini-360 DC-DC Buck converter [package=THT]
  Track_Power_7-30V = Power plug
  U1 = DB107 [package=THT]
  C1-103 = Ceramic Capacitor [capacitance=10nF voltage=35V package="100 mil [THT, multilayer]"]
  U3 = 555 Timer [package="DIP8 [THT]"]
  C2 = Electrolytic Capacitor [capacitance=10µF voltage=35V package="100 mil [THT, electrolytic]"]
  R5 = Resistor [tolerance=±5% power=0.25W resistance=47k package=THT]
  R6 = Resistor [tolerance=±5% power=0.25W resistance=1k package=THT]
  D1_1N4148 = Diode [package=diode-1n4148]
  VR1_Trimpot = Trimpot-3296-Lay [part_number="P104 (100K)" package=3386u]
  C4-104 = Ceramic Capacitor [capacitance=100nF voltage=35V package="100 mil [THT, multilayer]"]
  Q1_G1/D2/S3_IRLZ44N = Basic FET N-Channel [package="D2Pak [SMD]"]
  R7 = Resistor [tolerance=±5% power=0.25W resistance=10k package=THT]

nets:
  N1: M4.GND, Q1_G1/D2/S3_IRLZ44N.drain
  N2: M4.VCC, U2.OUT+, U3.Reset, U3.Vcc_Supply_Voltage, R5.Pin_1, C4-104.0
  N3: U2.IN-, U1.Pin_4
  N4: U2.IN+, U1.Pin_3
  N5: U2.OUT-, C1-103.0, U3.Ground, C2.-, C4-104.1, Q1_G1/D2/S3_IRLZ44N.source, R7.Pin_0
  N6: Track_Power_7-30V.VCC, U1.Pin_2
  N7: Track_Power_7-30V.GND, U1.Pin_1
  N8: C1-103.1, U3.Control_Voltage
  N9: U3.Trigger, U3.Threshold, C2.+, VR1_Trimpot.CW
  N10: U3.Output, R6.Pin_0
  N11: U3.Discharge, R5.Pin_0, D1_1N4148.C, VR1_Trimpot.CCW
  N12: R6.Pin_1, Q1_G1/D2/S3_IRLZ44N.Gate, R7.Pin_1
  N13: D1_1N4148.A, VR1_Trimpot.WIPER

notes:
  Input Voltage 9 - 24 Volts AC/DC
  Buck Converter Set to output 5 Volts
  Modified Atomizer Circuit to simulate Chuff
  Atomizer
  Atomizer Circuit Board
  Polarity does not matter
  Connect to Purple
  Connect to Yellow
  Connect to Red
  Connect to Orange
  KBP307 Bridge Rectifier
  *** NOTE  Running on less that 9 volts will give unexpected results, or no results at all

custom parts:
  seeed grove atomizer v1.0: Grove - Water Atomization is a perfect module for you to quickly DIY a humidifier with Arduino. You can also develop more advanced and interesting projects with digital scent technology and any other situations in which atomization required.
  Mini-360 DC-DC Buck converter: Mini-360 DC-DC Buck converter. Tiny buck step down voltage converter, input voltage 4.75 to 23V output 1 to 17V adjustable. Available from ebay and the like.
  Power plug: power plug
  DB107: Bridge rectifier
  Trimpot-3296-Lay: Trimpot 3296 / 25 turn lying 90 degree
