# Fritzing sketch Atomizer Chuff 555 (saved by Fritzing 1.0.6)

parts:
  M13 = seeed grove atomizer v1.0
  Power_plug2 = Power plug
  U12 = Mini-360 DC-DC Buck converter [package=THT]
  M4 = seeed grove atomizer v1.0
  U2 = Mini-360 DC-DC Buck converter [package=THT]
  U11 = DB107 [package=THT]
  Track_Power_7-30V = Power plug
  U1 = DB107 [package=THT]
  C1-103 = Ceramic Capacitor [capacitance=10nF voltage=35V package="100 mil [THT, multilayer]"]
  U3 = 555 Timer [package="DIP8 [THT]"]
  C2 = Electrolytic Capacitor [capacitance=10µF voltage=35V package="100 mil [THT, electrolytic]"]
  R5 = Resistor [tolerance=±5% power=0.25W resistance=47k package=THT]
  R6 = Resistor [tolerance=±5% power=0.25W resistance=1k package=THT]
  D1_1N4148 = Diode [package=diode-1n4148]
  VR1_Trimpot = Trimpot-3296-Lay [part_number="P104 (100K)" package=3386u]
  C4-104 = Ceramic Capacitor [capacitance=100nF voltage=35V package="100 mil [THT, multilayer]"]
  Q1_G1/D2/S3_IRLZ44N = Basic FET N-Channel [package="D2Pak [SMD]"]

nets:
  N1: M13.GND, U12.OUT-
  N2: M13.VCC, U12.OUT+
  N3: Power_plug2.VCC, U11.Pin_2
  N4: Power_plug2.GND, U11.Pin_1
  N5: U12.IN-, U11.Pin_4
  N6: U12.IN+, U11.Pin_3
  N7: M4.GND, Q1_G1/D2/S3_IRLZ44N.drain
  N8: M4.VCC, U2.OUT+, U3.Reset, U3.Vcc_Supply_Voltage, R5.Pin_1, C4-104.0
  N9: U2.IN-, U1.Pin_4
  N10: U2.IN+, U1.Pin_3
  N11: U2.OUT-, C1-103.0, U3.Ground, C2.-, C4-104.1, Q1_G1/D2/S3_IRLZ44N.source
  N12: Track_Power_7-30V.VCC, U1.Pin_2
  N13: Track_Power_7-30V.GND, U1.Pin_1
  N14: C1-103.1, U3.Control_Voltage
  N15: U3.Trigger, U3.Threshold, C2.+, VR1_Trimpot.CW
  N16: U3.Output, R6.Pin_0
  N17: U3.Discharge, R5.Pin_0, D1_1N4148.C, VR1_Trimpot.CCW
  N18: R6.Pin_1, Q1_G1/D2/S3_IRLZ44N.Gate
  N19: D1_1N4148.A, VR1_Trimpot.WIPER

notes:
  Buck Converter Set to output 5 Volts
  Input Voltage 9 - 24 Volts AC/DC
  Atomizer
  Modified Atomizer Circuit to simulate Chuff
  Atomizer Circuit Board
  Original Atomizer Circuit
  KBP307 Bridge Rectifier
  Polarity does not matter
  Connect to Purple
  Connect to Yellow
  Connect to Red
  Connect to Orange
  *** NOTE  Running on less that 9 volts will give unexpected results, or no results at all

custom parts:
  seeed grove atomizer v1.0: Grove - Water Atomization is a perfect module for you to quickly DIY a humidifier with Arduino. You can also develop more advanced and interesting projects with digital scent technology and any other situations in which atomization required.
  Power plug: power plug
  Mini-360 DC-DC Buck converter: Mini-360 DC-DC Buck converter. Tiny buck step down voltage converter, input voltage 4.75 to 23V output 1 to 17V adjustable. Available from ebay and the like.
  DB107: Bridge rectifier
  Trimpot-3296-Lay: Trimpot 3296 / 25 turn lying 90 degree
